// Digital circuit hardware.dig as structural Verilog
module hardware (
  input  clk,
  input  in_2,
  input  in_3,
  input  [15:0] in_4,
  input  in_5,
  input  in_6,
  input  [15:0] in_7,
  input  [3:0] in_8
);

  wire control_1_p7, control_1_p9, control_1_p10, InstrEx, InstrL, jumpdecider_1_jmp, PC_ovf, RTW;
  wire [3:0] alu_1_fl, control_1_p6, Flags_q, RA, RT;
  wire [7:0] control_1_p8, registerfile_1_da, registerfile_1_da_2;
  wire [15:0] alu_1_rdata, control_1_p11, InstrReg_q, PC_out, ramdualport_1_d, registerfile_1_db;

  Counter Phase (.en(1'b1), .C(clk), .clr(1'b0), .out(InstrEx));  // open: ovf
  not not_1 (InstrL, InstrEx);
  CounterPreset #(.Bits(16)) PC (
    .en(InstrL), .C(clk), .dir(in_2), .in(in_4), .ld(in_3), .clr(in_5), .out(PC_out), .ovf(PC_ovf));
  // Probe on PC_ovf
  RAMDualPort #(.AddrBits(16), .isProgramMemory("true"), .Bits(16)) ramdualport_1 (
    .A(PC_out), .Din(in_7), .str(in_6), .C(clk), .ld(1'b1), .D(ramdualport_1_d));
  Register #(.Bits(16)) InstrReg (.D(ramdualport_1_d), .C(clk), .en(InstrL), .Q(InstrReg_q));
  RegisterFile #(.AddrBits(4), .Bits(16)) registerfile_1 (
    .Din(control_1_p11), .we(RTW), .Rw(RT), .C(clk), .Ra(RT), .Rb(RA),
    .Da({registerfile_1_da_2, registerfile_1_da}), .Db(registerfile_1_db));
  // Probe on InstrReg_q
  // control control_1: pin names not known; wires that end beside it: InstrReg_q, InstrEx, RT, RTW, RA, control_1_p6, control_1_p7, control_1_p8, control_1_p9, control_1_p10, control_1_p11
  alu alu_1 (
    .Op(control_1_p6), .TData({registerfile_1_da_2, registerfile_1_da}), .AData(registerfile_1_db),
    .RData(alu_1_rdata), .Fl(alu_1_fl));
  assign control_1_p11 = control_1_p7 ? alu_1_rdata : 16'bz;  // Driver driver_1
  // Probe on control_1_p8
  assign control_1_p11 = control_1_p9 ? {registerfile_1_da_2, control_1_p8} : 16'bz;  // Driver driver_2
  assign control_1_p11 = control_1_p10 ? {control_1_p8, registerfile_1_da} : 16'bz;  // Driver driver_3
  // Probe on control_1_p11
  Register #(.Bits(4)) Flags (.D(alu_1_fl), .C(clk), .en(control_1_p7), .Q(Flags_q));
  jumpDecider jumpdecider_1 (.JT(in_8), .Fl(Flags_q), .Jmp(jumpdecider_1_jmp));
  LED led_1 (.in(Flags_q[0]));
  LED led_2 (.in(Flags_q[1]));
  LED led_3 (.in(Flags_q[2]));
  LED led_4 (.in(Flags_q[3]));
  LED led_5 (.in(jumpdecider_1_jmp));

  // Notes on the sheet:
  //   Imm
  //   Data
  //   fN
  //   fZ
  //   fC
  //   fO
  //   Jmp
endmodule
